// Logisim project cpu.circ as structural Verilog: 4 circuits, main circuit main
module main (
  input  [31:0] INSTRUCTION,
  input  CLOCK,
  output [31:0] FETCH_ADDRESS,
  output [31:0] s0_Value,
  output [31:0] s1_Value,
  output [31:0] s2_Value,
  output [31:0] ra_Value,
  output [31:0] HI_Value,
  output [31:0] LO_Value
);

  wire ALUSrc, and_2_out, and_4_out, and_link, Beq, Bne, Branch, div, equal, ExtOp, jr, Jump, lui, MEM_p1,
       MemToReg, MemWrite, mfhi, mflo, mul, mul_or_div, multiplexer_14_out, noop, not_1_out, RegDst,
       RegWrite, Shift, signed_over, swinc, take_branch, WriteReg;
  wire [1:0] multiplexer_3_out;
  wire [2:0] OpUnit;
  wire [3:0] ALU_Ctr;
  wire [4:0] multiplexer_9_out, rd, rs, rt, shamt, target_reg;
  wire [5:0] funct, opcode;
  wire [15:0] imm;
  wire [25:0] addr;
  wire [27:0] bit_extender_1_out, shifter_1_out;
  wire [31:0] adder_1_out, adder_2_out, arg2, EXECUTE, ext, INST, multiplexer_1_out, multiplexer_2_out,
       multiplexer_5_out, multiplexer_11_out, multiplexer_12_out, new_addr, read, register_write_data, Res1,
       Res2, rs_val, rt_val, shamt_extend, shifter_2_out, write_data;

  assign bit_extender_1_out = {{2{1'b0}}, addr};  // Bit_Extender bit_extender_1
  Register #(.width(32)) PC (.D(new_addr), .Q(FETCH_ADDRESS), .clk(CLOCK));  // open: en, clr
  instr_split instr_split (
    .in_1(EXECUTE), .funct(funct), .shamt(shamt), .rd(rd), .imm(imm), .addr(addr), .rt(rt), .rs(rs),
    .opcode(opcode));
  assign shamt_extend = {{27{1'b0}}, shamt};  // Bit_Extender bit_extender_2
  if_noop if_noop_1 (.beq(Beq), .equal(equal), .bne(Bne), .jump(Jump), .insert_noop(noop));
  and and_1 (jr, Jump, ~ALUSrc);  // AND_Gate
  Shifter #(.width(28)) shifter_1 (.in(bit_extender_1_out), .\dist (5'b00010), .out(shifter_1_out));
  Adder #(.width(32)) adder_1 (.a(FETCH_ADDRESS), .b(32'h4), .out(adder_1_out));  // open: cin, cout
  Shifter #(.width(32)) shifter_2 (.in(ext), .\dist (5'b00010), .out(shifter_2_out));
  Multiplexer #(.width(32)) multiplexer_1 (
    .in0({FETCH_ADDRESS[31:28], shifter_1_out}), .in1(rs_val), .out(multiplexer_1_out), .sel(jr));  // open: en
  Adder #(.width(32)) adder_2 (.a(FETCH_ADDRESS), .b(shifter_2_out), .out(adder_2_out));  // open: cin, cout
  Multiplexer #(.width(32)) multiplexer_2 (
    .in0(Res1), .in1({imm, {16{1'b0}}}), .out(multiplexer_2_out), .sel(lui));  // open: en
  Multiplexer #(.width(2)) multiplexer_3 (
    .in0({mflo, mfhi}), .in1(2'b11), .out(multiplexer_3_out), .sel(MemToReg));  // open: en
  // Probe on INSTRUCTION
  Multiplexer #(.width(32)) multiplexer_4 (
    .in0(multiplexer_1_out), .in1(multiplexer_5_out), .out(new_addr), .sel(not_1_out));  // open: en
  Multiplexer #(.width(32)) multiplexer_5 (
    .in0(adder_1_out), .in1(adder_2_out), .out(multiplexer_5_out), .sel(take_branch));  // open: en
  not not_1 (not_1_out, Jump);
  Multiplexer #(.select(2), .width(32)) multiplexer_6 (
    .in0(write_data), .in1(HI_Value), .in2(LO_Value), .in3(read), .out(register_write_data),
    .sel(multiplexer_3_out));  // open: en
  Multiplexer #(.width(32)) multiplexer_7 (.in0(INSTRUCTION), .in1({32{1'b0}}), .out(INST), .sel(noop));  // open: en
  // Probe on INST
  Multiplexer #(.width(32)) multiplexer_8 (
    .in0(multiplexer_2_out), .in1(FETCH_ADDRESS), .out(write_data), .sel(and_link));  // open: en
  Multiplexer #(.select(2), .width(5), .enable("false")) multiplexer_9 (
    .in0(rt), .in1(rd), .in2({5{1'b1}}), .in3({5{1'b1}}), .out(multiplexer_9_out), .sel({and_link, RegDst}));
  or or_1 (mul_or_div, mul, div);
  Comparator #(.width(4), .mode("unsigned")) comparator_1 (.a(ALU_Ctr), .b(4'b0011), .eq(mul));  // open: gt, lt
  Comparator #(.width(4)) comparator_2 (.a(ALU_Ctr), .b(4'b0100), .eq(div));  // open: gt, lt
  regfile_main main_1 (
    .Read_Register_1(rs), .Read_Register_2(rt), .Write_Register(target_reg),
    .Write_Data(register_write_data), .Write_Enable(WriteReg), .Clock(CLOCK), .Read_Data_1(rs_val),
    .Read_Data_2(rt_val), .s0_Value(s0_Value), .s1_Value(s1_Value), .s2_Value(s2_Value), .ra_Value(ra_Value));
  Multiplexer #(.width(5)) multiplexer_10 (
    .in0(multiplexer_9_out), .in1(rs), .out(target_reg), .sel(swinc));  // open: en
  Multiplexer #(.width(32), .enable("false")) multiplexer_11 (
    .in0(rs_val), .in1(rt_val), .out(multiplexer_11_out), .sel(Shift));
  Register #(.width(32)) HI (.D(Res2), .en(mul_or_div), .Q(HI_Value), .clk(CLOCK));  // open: clr
  Register #(.width(32)) LO (.D(Res1), .en(mul_or_div), .Q(LO_Value), .clk(CLOCK));  // open: clr
  alu_main main_2 (
    .Switch(ALU_Ctr), .X(multiplexer_11_out), .Equal(equal), .Result(Res1), .Signed_Overflow(signed_over),
    .Y(arg2), .Result_2(Res2));
  control control_1 (
    .opcode(opcode), .funct(funct), .Lui(lui), .And_Link(and_link), .Op_Unit(OpUnit), .Bne(Bne), .Beq(Beq),
    .RegWr(RegWrite), .MemToReg(MemToReg), .MemWr(MemWrite), .ALU_Ctr(ALU_Ctr), .ALUSrc(ALUSrc),
    .ExtOp(ExtOp), .RegDst(RegDst), .Branch(Branch), .Jump(Jump), .Shift(Shift));
  LED led_1 (.in(signed_over));
  Comparator #(.width(4), .mode("unsigned")) comparator_3 (.a(ALU_Ctr), .b(4'b1101), .eq(mfhi));  // open: gt, lt
  Comparator #(.width(4)) comparator_4 (.a(ALU_Ctr), .b(4'b1110), .eq(mflo));  // open: gt, lt
  // mem_main MEM: pin names not known; wires that end beside it: MEM_p1, Res1, rt_val, MemWrite, CLOCK, OpUnit, read
  and and_2 (and_2_out, ExtOp, imm[15]);
  assign ext = {{16{and_2_out}}, imm};  // Bit_Extender bit_extender_3
  Register #(.width(32)) First_Stage_Pipeline (.D(INST), .Q(EXECUTE), .clk(CLOCK));  // open: en, clr
  // Probe on EXECUTE
  Multiplexer #(.width(32), .enable("false")) multiplexer_12 (
    .in0(rt_val), .in1(ext), .out(multiplexer_12_out), .sel(ALUSrc));
  and and_3 (swinc, MemWrite, RegWrite);
  Multiplexer multiplexer_13 (.in0(RegWrite), .in1(take_branch), .out(WriteReg), .sel(and_4_out));  // open: en
  and and_4 (and_4_out, Branch, and_link);
  Multiplexer multiplexer_14 (.in0(Bne), .in1(Beq), .out(multiplexer_14_out), .sel(equal));  // open: en
  and and_5 (take_branch, multiplexer_14_out, Branch);
  Multiplexer #(.width(32), .enable("false")) multiplexer_15 (
    .in0(multiplexer_12_out), .in1(shamt_extend), .out(arg2), .sel(Shift));

  // Other names for the same wires on the sheet: clk = CLOCK; high[31:0] = HI_Value; low[31:0] = LO_Value;
  //   fetch_addr[31:0] = FETCH_ADDRESS; pc___4[31:0] = FETCH_ADDRESS; ra[31:0] = ra_Value; WriteData[31:0] = rt_val;
  //   s0[31:0] = s0_Value; s1[31:0] = s1_Value; s2[31:0] = s2_Value

  // Notes on the sheet:
  //   Do we need to insert a noop?
  //   Output
  //   These are outputs/inputs from run.circ
  //   PC Logic
  //   Inputs
  //   These are DEBUG/TEST outputs from your circuit.
  //   Select Write Register
  //   Primary Datapath
endmodule

module control (
  input  [5:0] opcode,
  input  [5:0] funct,
  output Lui,
  output And_Link,
  output [2:0] Op_Unit,
  output Bne,
  output Beq,
  output RegWr,
  output MemToReg,
  output MemWr,
  output [3:0] ALU_Ctr,
  output ALUSrc,
  output ExtOp,
  output RegDst,
  output Branch,
  output Jump,
  output Shift
);

  wire comparator_1_eq;
  wire [4:0] funct_high, funct_low, opcode_high, opcode_low;
  wire [19:0] funct_map, multiplexer_1_out, multiplexer_2_out, multiplexer_4_out, multiplexer_5_out,
       opcode_map;

  Demultiplexer #(.width(5), .enable("false")) demultiplexer_1 (
    .out0(opcode_low), .out1(opcode_high), .in(opcode[4:0]), .sel(opcode[5]));
  Demultiplexer #(.width(5), .enable("false")) demultiplexer_2 (
    .out0(funct_low), .out1(funct_high), .in(funct[4:0]), .sel(funct[5]));
  // Probe on {Shift, Jump, Branch, RegDst, ExtOp, ALUSrc, ALU_Ctr, MemWr, MemToReg, RegWr, Beq, Bne, Op_Unit, And_Link, Lui}
  Multiplexer #(.select(5), .width(20)) multiplexer_1 (
    .in0({20{1'b0}}), .in2(20'h44000), .in3(20'h44082), .in4(20'h2bc40), .in5(20'h2bc20), .in8(20'hd480),
    .in9(20'hd880), .in10(20'hec80), .in12(20'h6480), .in13(20'h6880), .in15(20'h7c81), .in20(20'h2bcc2),
    .out(multiplexer_1_out), .sel(opcode_low));  // open: in1, in6, in7, in11, in14, in16, in17, in18, in19, in21, in22, in23, in24, in25, in26, in27, in28, in29, in30, in31, en
  Multiplexer #(.select(5), .width(20)) multiplexer_2 (
    .in0(20'hd984), .in3(20'hd99c), .in4(20'hd980), .in5(20'hd98c), .in8(20'hda04), .in9(20'hda0c),
    .in11(20'hda1c), .in12(20'hda9c), .out(multiplexer_2_out), .sel(opcode_high));  // open: in1, in2, in6, in7, in10, in13, in14, in15, in16, in17, in18, in19, in20, in21, in22, in23, in24, in25, in26, in27, in28, in29, in30, in31, en
  Multiplexer #(.width(20)) multiplexer_3 (
    .in0(multiplexer_1_out), .in1(multiplexer_2_out), .out(opcode_map), .sel(opcode[5]));  // open: en
  Comparator #(.width(6)) comparator_1 (.a(opcode), .b({6{1'b0}}), .eq(comparator_1_eq));  // open: gt, lt
  Multiplexer #(.select(5), .width(20)) multiplexer_4 (
    .in0(20'h90080), .in2(20'h90480), .in3(20'h90880), .in8(20'h40000), .in16(20'h13480), .in18(20'h13880),
    .in25(20'hc00), .in27(20'h1000), .out(multiplexer_4_out), .sel(funct_low));  // open: in1, in4, in5, in6, in7, in9, in10, in11, in12, in13, in14, in15, in17, in19, in20, in21, in22, in23, in24, in26, in28, in29, in30, in31, en
  Multiplexer #(.select(5), .width(20)) multiplexer_5 (
    .in0(20'h11480), .in1(20'h11880), .in2(20'h11c80), .in3(20'h12080), .in4(20'h12480), .in5(20'h12880),
    .in10(20'h12c80), .in11(20'h13080), .out(multiplexer_5_out), .sel(funct_high));  // open: in6, in7, in8, in9, in12, in13, in14, in15, in16, in17, in18, in19, in20, in21, in22, in23, in24, in25, in26, in27, in28, in29, in30, in31, en
  Multiplexer #(.width(20)) multiplexer_6 (
    .in0(opcode_map), .in1(funct_map),
    .out({Shift, Jump, Branch, RegDst, ExtOp, ALUSrc, ALU_Ctr, MemWr, MemToReg, RegWr, Beq, Bne, Op_Unit, And_Link, Lui}),
    .sel(comparator_1_eq));  // open: en
  Multiplexer #(.width(20)) multiplexer_7 (
    .in0(multiplexer_4_out), .in1(multiplexer_5_out), .out(funct_map), .sel(funct[5]));  // open: en

  // Other names for the same wires on the sheet: Control_Out[19:0] = {Shift, Jump, Branch, RegDst, ExtOp, ALUSrc, ALU_Ctr, MemWr, MemToReg, RegWr, Beq, Bne, Op_Unit, And_Link, Lui};
  //   funct_t[5:0] = funct; top_funct_bit = funct[5]; opcode_t[5:0] = opcode; top_opcode_bit = opcode[5]

  // Notes on the sheet:
  //   All 64 possible opcodes and functs are mapped
  //   Simulates 64-input MUX
  //   using 2 32-input muxes (max mux size in Logisim)
  //   Ex: Bit 18 (Jump) is set on a jump instruction
  //   Control Out is a 20-bit number containing all control signals needed.
  //   Control signals are determined by funct if R-type instruction
endmodule

module instr_split (
  input  [31:0] in_1,
  output [5:0] funct,
  output [4:0] shamt,
  output [4:0] rd,
  output [15:0] imm,
  output [25:0] addr,
  output [4:0] rt,
  output [4:0] rs,
  output [5:0] opcode
);


  assign addr = in_1[25:0];
  assign funct = in_1[5:0];
  assign imm = in_1[15:0];
  assign opcode = in_1[31:26];
  assign rd = in_1[15:11];
  assign rs = in_1[25:21];
  assign rt = in_1[20:16];
  assign shamt = in_1[10:6];

  // Notes on the sheet:
  //   r-type
endmodule

module if_noop (
  input  beq,
  input  equal,
  input  bne,
  input  jump,
  output insert_noop
);

  wire and_1_out, and_2_out, or_1_out;

  and and_1 (and_1_out, beq, equal);
  and and_2 (and_2_out, ~equal, bne);  // AND_Gate
  or or_1 (or_1_out, and_1_out, and_2_out);
  or or_2 (insert_noop, or_1_out, jump);
endmodule
