// Logisim project alu.circ as structural Verilog: 2 circuits, main circuit main
module main (
  input  [31:0] X,
  input  [31:0] Y,
  input  [3:0] Switch,
  output Signed_Overflow,
  output Equal,
  output [31:0] Result,
  output [31:0] Result_2
);

  wire adder_1_cout, adder_2_cout, comparator_1_lt, comparator_2_lt, decoder_1_out5, decoder_1_out7,
       decoder_1_out8, is_div, is_mult, \signed , xor_1_out, Y_Negate;
  wire [4:0] bit_extender_1_out, bit_extender_2_out, bit_extender_3_out;
  wire [31:0] add, \and , div, div_2, mul, mul_2, multiplexer_2_out, multiplexer_3_out, negate_select_1_out,
       \or , sll, slt, sltu, sra, srl;

  Bit_Extender #(.in_width(32), .out_width(5)) bit_extender_1 (.in(Y), .out(bit_extender_1_out));
  Bit_Extender #(.in_width(32), .out_width(5)) bit_extender_2 (.in(Y), .out(bit_extender_2_out));
  Bit_Extender #(.in_width(32), .out_width(5)) bit_extender_3 (.in(Y), .out(bit_extender_3_out));
  Shifter #(.width(32)) shifter_1 (.in(X), .\dist (bit_extender_1_out), .out(sll));
  Shifter #(.width(32), .shift("lr")) shifter_2 (.in(X), .\dist (bit_extender_2_out), .out(srl));
  Shifter #(.width(32), .shift("ar")) shifter_3 (.in(X), .\dist (bit_extender_3_out), .out(sra));
  Multiplexer #(.select(4), .width(32), .disabled(0)) multiplexer_1 (
    .in0(sll), .in1(srl), .in2(sra), .in3(mul), .in4(div), .in5(add), .in6(add), .in7(add), .in8(add),
    .in9(\and ), .in10(\or ), .in11(slt), .in12(sltu), .in13({32{1'b0}}), .in14({32{1'b0}}),
    .in15({32{1'b0}}), .out(Result), .sel(Switch));  // open: en
  Multiplier #(.width(32)) multiplier_1 (.a(X), .b(Y), .out(mul), .cout(mul_2));  // open: cin
  Divider #(.width(32)) divider_1 (.a(X), .b(Y), .out(div), .rem(div_2));  // open: upper
  Decoder #(.select(4)) decoder_1 (
    .out3(is_mult), .out4(is_div), .out5(decoder_1_out5), .out7(decoder_1_out7), .out8(decoder_1_out8),
    .sel(Switch));  // open: out0, out1, out2, out6, out9, out10, out11, out12, out13, out14, out15, en
  or or_1 (\signed , decoder_1_out5, decoder_1_out7);
  or or_2 (Y_Negate, decoder_1_out7, decoder_1_out8);
  Comparator #(.width(32)) comparator_1 (.a(X), .b(Y), .eq(Equal), .lt(comparator_1_lt));  // open: gt
  assign slt = {{31{1'b0}}, comparator_1_lt};  // Bit_Extender bit_extender_4
  Comparator #(.width(32), .mode("unsigned")) comparator_2 (.a(X), .b(Y), .lt(comparator_2_lt));  // open: gt, eq
  assign sltu = {{31{1'b0}}, comparator_2_lt};  // Bit_Extender bit_extender_5
  assign \and  = X & Y;  // AND_Gate and_1, 32 bits wide
  assign \or  = X | Y;  // OR_Gate or_3, 32 bits wide
  negate_select negate_select_1 (.Input(Y), .Negate(Y_Negate), .out(negate_select_1_out));
  Multiplexer #(.width(32)) multiplexer_2 (
    .in0({32{1'b0}}), .in1(mul_2), .out(multiplexer_2_out), .sel(is_mult));  // open: en
  Multiplexer #(.width(32)) multiplexer_3 (
    .in0({32{1'b0}}), .in1(div_2), .out(multiplexer_3_out), .sel(is_div));  // open: en
  Adder #(.width(31)) adder_1 (
    .a(X[30:0]), .b(negate_select_1_out[30:0]), .out(add[30:0]), .cout(adder_1_cout));  // open: cin
  Adder #(.width(1)) adder_2 (
    .a(X[31]), .b(negate_select_1_out[31]), .out(add[31]), .cin(adder_1_cout), .cout(adder_2_cout));
  assign Result_2 = multiplexer_2_out | multiplexer_3_out;  // OR_Gate or_4, 32 bits wide
  xor xor_1 (xor_1_out, adder_1_cout, adder_2_cout);
  and and_2 (Signed_Overflow, xor_1_out, \signed );

  // Other names for the same wires on the sheet: overflow = Signed_Overflow; S[3:0] = Switch

  // Notes on the sheet:
  //   INPUTS to your circuit
  //   Shifts Left Logical
  //   Shift Right Logical
  //   Shift Right Arithmetic
  //   Multiply Unsigned
  //   Divide Unsigned
  //   DON'T CHANGE THE LOCATIONS OF THE INPUTS AND OUTPUTS!
  //   Tests Equal/Set Less Than
  //   Set Less Than Unsigned
  //   AND
  //   OR
  //   OUTPUTS from your circuit
  //   Add
  //   Mult/Div Result 2
endmodule

module negate_select (
  input  [31:0] Input,
  input  Negate,
  output [31:0] out
);

  wire [31:0] negator_1_out;

  Negator #(.width(32)) negator_1 (.in(Input), .out(negator_1_out));
  Multiplexer #(.width(32)) multiplexer_1 (.in0(Input), .in1(negator_1_out), .out(out), .sel(Negate));  // open: en
endmodule
