// Logisim project regfile.circ as structural Verilog: 1 circuit, main circuit main
module main (
  input  [4:0] Read_Register_1,
  input  [4:0] Read_Register_2,
  input  [4:0] Write_Register,
  input  [31:0] Write_Data,
  input  Write_Enable,
  input  Clock,
  output [31:0] s0_Value,
  output [31:0] s1_Value,
  output [31:0] s2_Value,
  output [31:0] ra_Value,
  output [31:0] Read_Data_1,
  output [31:0] Read_Data_2
);

  wire decoder_1_out0, decoder_1_out1, decoder_1_out2, decoder_1_out3, decoder_1_out4, decoder_1_out5,
       decoder_1_out6, decoder_1_out7, decoder_1_out8, decoder_1_out9, decoder_1_out10, decoder_1_out11,
       decoder_1_out12, decoder_1_out13, decoder_1_out14, decoder_1_out15, decoder_1_out16, decoder_1_out17,
       decoder_1_out18, decoder_1_out19, decoder_1_out20, decoder_1_out21, decoder_1_out22, decoder_1_out23,
       decoder_1_out24, decoder_1_out25, decoder_1_out26, decoder_1_out27, decoder_1_out28, decoder_1_out29,
       decoder_1_out30, decoder_1_out31, w0, w1, w2, w3, w4, w5, w6, w7, w8, w9, w10, w11, w12, w13, w14,
       w15, w16, w17, w18, w19, w20, w21, w22, w23, w24, w25, w26, w27, w28, w29, w30, w31;
  wire [31:0] _0, _1, _2, _3, _4, _5, _6, _7, _8, _9, _10, _11, _12, _13, _14, _15, _19, _20, _21, _22, _23,
       _24, _25, _26, _27, _28, _29, _30;

  Multiplexer #(.select(5), .width(32)) multiplexer_1 (
    .in0(_0), .in1(_1), .in2(_2), .in3(_3), .in4(_4), .in5(_5), .in6(_6), .in7(_7), .in8(_8), .in9(_9),
    .in10(_10), .in11(_11), .in12(_12), .in13(_13), .in14(_14), .in15(_15), .in16(s0_Value), .in17(s1_Value),
    .in18(s2_Value), .in19(_19), .in20(_20), .in21(_21), .in22(_22), .in23(_23), .in24(_24), .in25(_25),
    .in26(_26), .in27(_27), .in28(_28), .in29(_29), .in30(_30), .in31(ra_Value), .out(Read_Data_1),
    .sel(Read_Register_1), .en(1'b1));
  Multiplexer #(.select(5), .width(32)) multiplexer_2 (
    .in0(_0), .in1(_1), .in2(_2), .in3(_3), .in4(_4), .in5(_5), .in6(_6), .in7(_7), .in8(_8), .in9(_9),
    .in10(_10), .in11(_11), .in12(_12), .in13(_13), .in14(_14), .in15(_15), .in16(s0_Value), .in17(s1_Value),
    .in18(s2_Value), .in19(_19), .in20(_20), .in21(_21), .in22(_22), .in23(_23), .in24(_24), .in25(_25),
    .in26(_26), .in27(_27), .in28(_28), .in29(_29), .in30(_30), .in31(ra_Value), .out(Read_Data_2),
    .sel(Read_Register_2), .en(1'b1));
  Decoder #(.select(5)) decoder_1 (
    .out0(decoder_1_out0), .out1(decoder_1_out1), .out2(decoder_1_out2), .out3(decoder_1_out3),
    .out4(decoder_1_out4), .out5(decoder_1_out5), .out6(decoder_1_out6), .out7(decoder_1_out7),
    .out8(decoder_1_out8), .out9(decoder_1_out9), .out10(decoder_1_out10), .out11(decoder_1_out11),
    .out12(decoder_1_out12), .out13(decoder_1_out13), .out14(decoder_1_out14), .out15(decoder_1_out15),
    .out16(decoder_1_out16), .out17(decoder_1_out17), .out18(decoder_1_out18), .out19(decoder_1_out19),
    .out20(decoder_1_out20), .out21(decoder_1_out21), .out22(decoder_1_out22), .out23(decoder_1_out23),
    .out24(decoder_1_out24), .out25(decoder_1_out25), .out26(decoder_1_out26), .out27(decoder_1_out27),
    .out28(decoder_1_out28), .out29(decoder_1_out29), .out30(decoder_1_out30), .out31(decoder_1_out31),
    .sel(Write_Register), .en(Write_Enable));
  and and_1 (w0, decoder_1_out0, Write_Enable);
  and and_2 (w1, decoder_1_out1, Write_Enable);
  and and_3 (w24, decoder_1_out24, Write_Enable);
  Register #(.width(32)) register_1 (.D(Write_Data), .en(w0), .Q(_0), .clk(Clock), .clr(1'b1));
  Register #(.width(32)) register_2 (.D(Write_Data), .en(w4), .Q(_4), .clk(Clock));  // open: clr
  Register #(.width(32)) register_3 (.D(Write_Data), .en(w8), .Q(_8), .clk(Clock));  // open: clr
  Register #(.width(32)) register_4 (.D(Write_Data), .en(w12), .Q(_12), .clk(Clock));  // open: clr
  Register #(.width(32)) register_5 (.D(Write_Data), .en(w16), .Q(s0_Value), .clk(Clock));  // open: clr
  Register #(.width(32)) register_6 (.D(Write_Data), .en(w20), .Q(_20), .clk(Clock));  // open: clr
  Register #(.width(32)) register_7 (.D(Write_Data), .en(w24), .Q(_24), .clk(Clock));  // open: clr
  Register #(.width(32)) register_8 (.D(Write_Data), .en(w28), .Q(_28), .clk(Clock));  // open: clr
  and and_4 (w13, decoder_1_out13, Write_Enable);
  and and_5 (w25, decoder_1_out25, Write_Enable);
  and and_6 (w2, decoder_1_out2, Write_Enable);
  and and_7 (w3, decoder_1_out3, Write_Enable);
  and and_8 (w14, decoder_1_out14, Write_Enable);
  and and_9 (w15, decoder_1_out15, Write_Enable);
  and and_10 (w26, decoder_1_out26, Write_Enable);
  and and_11 (w27, decoder_1_out27, Write_Enable);
  Register #(.width(32)) register_9 (.D(Write_Data), .en(w1), .Q(_1), .clk(Clock));  // open: clr
  Register #(.width(32)) register_10 (.D(Write_Data), .en(w5), .Q(_5), .clk(Clock));  // open: clr
  Register #(.width(32)) register_11 (.D(Write_Data), .en(w9), .Q(_9), .clk(Clock));  // open: clr
  Register #(.width(32)) register_12 (.D(Write_Data), .en(w13), .Q(_13), .clk(Clock));  // open: clr
  Register #(.width(32)) register_13 (.D(Write_Data), .en(w17), .Q(s1_Value), .clk(Clock));  // open: clr
  Register #(.width(32)) register_14 (.D(Write_Data), .en(w21), .Q(_21), .clk(Clock));  // open: clr
  Register #(.width(32)) register_15 (.D(Write_Data), .en(w25), .Q(_25), .clk(Clock));  // open: clr
  Register #(.width(32)) register_16 (.D(Write_Data), .en(w29), .Q(_29), .clk(Clock));  // open: clr
  and and_12 (w4, decoder_1_out4, Write_Enable);
  and and_13 (w16, decoder_1_out16, Write_Enable);
  and and_14 (w17, decoder_1_out17, Write_Enable);
  and and_15 (w28, decoder_1_out28, Write_Enable);
  and and_16 (w29, decoder_1_out29, Write_Enable);
  and and_17 (w5, decoder_1_out5, Write_Enable);
  and and_18 (w6, decoder_1_out6, Write_Enable);
  and and_19 (w7, decoder_1_out7, Write_Enable);
  and and_20 (w18, decoder_1_out18, Write_Enable);
  and and_21 (w19, decoder_1_out19, Write_Enable);
  and and_22 (w30, decoder_1_out30, Write_Enable);
  and and_23 (w31, decoder_1_out31, Write_Enable);
  Register #(.width(32)) register_17 (.D(Write_Data), .en(w2), .Q(_2), .clk(Clock));  // open: clr
  Register #(.width(32)) register_18 (.D(Write_Data), .en(w6), .Q(_6), .clk(Clock));  // open: clr
  Register #(.width(32)) register_19 (.D(Write_Data), .en(w10), .Q(_10), .clk(Clock));  // open: clr
  Register #(.width(32)) register_20 (.D(Write_Data), .en(w14), .Q(_14), .clk(Clock));  // open: clr
  Register #(.width(32)) register_21 (.D(Write_Data), .en(w18), .Q(s2_Value), .clk(Clock));  // open: clr
  Register #(.width(32)) register_22 (.D(Write_Data), .en(w22), .Q(_22), .clk(Clock));  // open: clr
  Register #(.width(32)) register_23 (.D(Write_Data), .en(w26), .Q(_26), .clk(Clock));  // open: clr
  Register #(.width(32)) register_24 (.D(Write_Data), .en(w30), .Q(_30), .clk(Clock));  // open: clr
  and and_24 (w8, decoder_1_out8, Write_Enable);
  and and_25 (w9, decoder_1_out9, Write_Enable);
  and and_26 (w10, decoder_1_out10, Write_Enable);
  and and_27 (w11, decoder_1_out11, Write_Enable);
  and and_28 (w12, decoder_1_out12, Write_Enable);
  and and_29 (w20, decoder_1_out20, Write_Enable);
  and and_30 (w21, decoder_1_out21, Write_Enable);
  and and_31 (w22, decoder_1_out22, Write_Enable);
  and and_32 (w23, decoder_1_out23, Write_Enable);
  Register #(.width(32)) register_25 (.D(Write_Data), .en(w3), .Q(_3), .clk(Clock));  // open: clr
  Register #(.width(32)) register_26 (.D(Write_Data), .en(w7), .Q(_7), .clk(Clock));  // open: clr
  Register #(.width(32)) register_27 (.D(Write_Data), .en(w11), .Q(_11), .clk(Clock));  // open: clr
  Register #(.width(32)) register_28 (.D(Write_Data), .en(w15), .Q(_15), .clk(Clock));  // open: clr
  Register #(.width(32)) register_29 (.D(Write_Data), .en(w19), .Q(_19), .clk(Clock));  // open: clr
  Register #(.width(32)) register_30 (.D(Write_Data), .en(w23), .Q(_23), .clk(Clock));  // open: clr
  Register #(.width(32)) register_31 (.D(Write_Data), .en(w27), .Q(_27), .clk(Clock));  // open: clr
  Register #(.width(32)) register_32 (.D(Write_Data), .en(w31), .Q(ra_Value), .clk(Clock));  // open: clr

  // Other names for the same wires on the sheet: _16[31:0] = s0_Value; _17[31:0] = s1_Value; _18[31:0] = s2_Value;
  //   _31[31:0] = ra_Value; clk = Clock; read_data1[31:0] = Read_Data_1; read_data2[31:0] = Read_Data_2;
  //   read_reg1[4:0] = Read_Register_1; read_reg2[4:0] = Read_Register_2; write_en = Write_Enable;
  //   write_reg[4:0] = Write_Register

  // Notes on the sheet:
  //   INPUTS to your circuit
  //   DON'T CHANGE THE LOCATIONS OF THE INPUTS AND OUTPUTS!
  //   These are DEBUG/TEST outputs from your circuit.
  //   OUTPUTS from your circuit
endmodule
